// Logisim project work_tunnel_version.circ as structural Verilog: 11 circuits, main circuit main
module ALU (
  input  [3:0] ALUM,
  input  [15:0] A,
  input  [15:0] B,
  output CF,
  output SF,
  output ZF,
  output OVF,
  output [31:0] oup,
  output ALUSBY
);

  wire adder_1_cout, and_2_out, clock_1_out, comparator_2_eq, comparator_4_eq, ISDIV, multiplexer_1_out,
       multiplexer_2_out, not_1_out, not_2_out, or_2_out, subtractor_1_bout, xnor_1_out, xor_1_out;
  wire [3:0] counter_1_q;
  wire [15:0] adder_1_out, div_1_quotent, div_1_remainder, divider_1_rem, divider_2_out, divider_2_rem,
       multiplier_1_cout, multiplier_1_out, multiplier_2_cout, multiplier_2_out, negator_1_out,
       subtractor_1_out;
  wire [31:0] negator_2_out, signxtnd_1_oup, signxtnd_2_oup;

  Divider #(.width(16)) divider_1 (.a(A), .b(B), .upper({16{1'b0}}), .rem(divider_1_rem));  // open: out
  DIV div_1 (
    .DIVISOR(B), .DIVIDEND(A), .START(ISDIV), .RESET(1'b0), .ALUSBY(ALUSBY), .QUOTENT(div_1_quotent),
    .REMAINDER(div_1_remainder));
  Negator #(.width(16)) negator_1 (.in(B), .out(negator_1_out));
  Multiplier #(.width(16)) multiplier_1 (
    .a(A), .b(B), .out(multiplier_1_out), .cin({16{1'b0}}), .cout(multiplier_1_cout));
  Multiplier #(.mode("twosComplement"), .width(16)) multiplier_2 (
    .a(A), .b(B), .out(multiplier_2_out), .cin({16{1'b0}}), .cout(multiplier_2_cout));
  Divider #(.mode("twosComplement"), .width(16)) divider_2 (
    .a(A), .b(B), .out(divider_2_out), .upper({16{1'b0}}), .rem(divider_2_rem));
  Multiplexer multiplexer_1 (.in0(B[15]), .in1(negator_1_out[15]), .out(multiplexer_1_out), .sel(ALUM[0]));
  Adder #(.width(16)) adder_1 (.a(A), .b(B), .out(adder_1_out), .cin(1'b0), .cout(adder_1_cout));
  Subtractor #(.width(16)) subtractor_1 (.a(A), .b(B), .out(subtractor_1_out), .bin(1'b0), .bout(subtractor_1_bout));
  xnor xnor_1 (xnor_1_out, A[15], multiplexer_1_out);
  SignXTND signxtnd_1 (.inp(adder_1_out), .oup(signxtnd_1_oup));
  Multiplexer multiplexer_2 (.in0(adder_1_cout), .in1(subtractor_1_bout), .out(multiplexer_2_out), .sel(ALUM[0]));
  SignXTND signxtnd_2 (.inp(subtractor_1_out), .oup(signxtnd_2_oup));
  or or_1 (CF, multiplexer_2_out, subtractor_1_bout);
  Negator #(.width(32)) negator_2 (.in({B, A}), .out(negator_2_out));
  Multiplexer #(.select(4), .width(32)) multiplexer_3 (
    .in0(signxtnd_1_oup), .in1(signxtnd_2_oup), .in10(negator_2_out),
    .in11({multiplier_1_cout, multiplier_1_out}), .in12({multiplier_2_cout, multiplier_2_out}),
    .in13({div_1_remainder, div_1_quotent}), .in14({divider_2_rem, divider_2_out}), .out(oup), .sel(ALUM));  // open: in2, in3, in4, in5, in6, in7, in8, in9, in15
  Comparator #(.mode("unsigned"), .width(4)) comparator_1 (.a(ALUM), .b(4'b1101), .eq(ISDIV));  // open: gt, lt
  Comparator #(.mode("unsigned"), .width(4)) comparator_2 (
    .a(ALUM), .b(4'b1110), .eq(comparator_2_eq));  // open: gt, lt
  Clock clock_1 (.out(clock_1_out));
  xor xor_1 (xor_1_out, oup[15], A[15]);
  not not_1 (not_1_out, or_2_out);
  Counter #(.max('hf), .width(4)) counter_1 (
    .clr(not_1_out), .load(and_2_out), .up(1'b0), .count(1'b1), .clk(clock_1_out), .D(4'b1111),
    .Q(counter_1_q));  // open: carry
  Comparator #(.mode("unsigned"), .width(16)) comparator_3 (.a({16{1'b0}}), .b(oup[15:0]), .eq(ZF));  // open: gt, lt
  and and_1 (OVF, xnor_1_out, xor_1_out);
  buf or_2 (or_2_out, comparator_2_eq);  // OR_Gate
  and and_2 (and_2_out, or_2_out, comparator_4_eq);
  not not_2 (not_2_out, comparator_4_eq);
  Comparator #(.mode("unsigned"), .width(4)) comparator_4 (
    .a(counter_1_q), .b(4'b0000), .eq(comparator_4_eq));  // open: gt, lt

  assign SF = oup[15];

  // Notes on the sheet:
  //   DIV
  //   IDIV
endmodule

module main (
);

  wire ALUSBY, ALUWE, and_1_out, ARWE, BSSEL, CF, clock_1_out, clock_2_out, clock_3_out, clock_4_out,
       clock_5_out, clock_6_out, clock_7_out, clock_8_out, clock_9_out, comparator_1_eq, CSWE, DRWE, DSEL,
       DSWE, IRWE, not_1_out, OVF, PCWE, RAMWE, RWE, SEGSEL, SF, XYWE, ZF;
  wire [1:0] ADRSEL, CS_OUT, DS_OUT, MEMSSEL, PCSEL, RWSEL, SEGMENT_IN, XSEL, YSEL;
  wire [3:0] ALUM;
  wire [4:0] DEST;
  wire [15:0] ADR_MUX, ALUREG_HIGH, ALUREG_LOW, AR_IN, AR_OUT, BSMUX, DR_HIGH, DR_LOW, MEMSSEL_OUT,
       multiplexer_5_out, multiplexer_7_out, multiplexer_8_out, PC_OUT, PCSEL_IN, regs_1_reg0, regs_1_x,
       regs_1_y, SES_OUT, SEU_OUT, XY_XOUT, XY_YOUT;
  wire [17:16] MEM_ADDR;
  wire [31:0] ALUOUT, ram_1_dout, RAM_MUX_OUT, ROMCONT;
  wire [31:16] IR_OUT;

  ROM #(.addrWidth(18), .dataWidth(32)) rom_1 (.addr({MEM_ADDR, ADR_MUX}), .data(ROMCONT));
  not not_1 (not_1_out, RAMWE);
  Clock clock_1 (.out(clock_1_out));
  RAM #(.addrWidth(18), .dataWidth(32)) ram_1 (
    .addr({MEM_ADDR, ADR_MUX}), .we(RAMWE), .oe(not_1_out), .clk(clock_1_out), .din({DR_HIGH, BSMUX}),
    .dout(ram_1_dout));
  Comparator #(.width(2)) comparator_1 (.a(2'b00), .b(CS_OUT), .eq(comparator_1_eq));  // open: gt, lt
  and and_1 (and_1_out, ~SEGSEL, comparator_1_eq);  // AND_Gate
  Multiplexer #(.width(32)) multiplexer_1 (.in0(ram_1_dout), .in1(ROMCONT), .out(RAM_MUX_OUT), .sel(and_1_out));
  Register #(.width(32)) IR (.D(RAM_MUX_OUT), .en(IRWE), .clk(clock_2_out), .Q({IR_OUT, AR_IN}));  // open: clr
  Clock clock_2 (.out(clock_2_out));
  Multiplexer #(.width(16)) multiplexer_2 (
    .in0(ALUREG_LOW), .in1({DR_LOW[15:8], ALUREG_LOW[7:0]}), .out(BSMUX), .sel(BSSEL));
  Multiplexer #(.select(2), .width(16)) multiplexer_3 (
    .in0(PC_OUT), .in1(AR_OUT), .in2(XY_YOUT), .out(ADR_MUX), .sel(ADRSEL));  // open: in3
  Multiplexer #(.select(2), .width(16)) multiplexer_4 (
    .in0(ALUOUT[15:0]), .in1(ALUREG_LOW), .in2(PC_OUT), .in3(AR_OUT), .out(PCSEL_IN));  // open: sel
  Multiplexer #(.select(2), .width(16)) multiplexer_5 (
    .in0(MEMSSEL_OUT), .in1(ALUREG_LOW), .in2(ALUREG_HIGH), .in3(AR_IN), .out(multiplexer_5_out), .sel(RWSEL));
  Register #(.width(32)) DR (.D(RAM_MUX_OUT), .en(DRWE), .clk(clock_3_out), .Q({DR_HIGH, DR_LOW}));  // open: clr
  Clock clock_3 (.out(clock_3_out));
  Multiplexer #(.select(2), .width(16)) multiplexer_6 (
    .in0(DR_LOW), .in1(SEU_OUT), .in2(SES_OUT), .out(MEMSSEL_OUT), .sel(MEMSSEL));  // open: in3
  REGS regs_1 (
    .AdrX(IR_OUT[25:21]), .AdrY(IR_OUT[20:16]), .Dest(DEST), .W(multiplexer_5_out), .RWE(RWE), .X(regs_1_x),
    .Y(regs_1_y), .REG0(regs_1_reg0));
  Clock clock_4 (.out(clock_4_out));
  Register #(.width(16)) PC (.D(PCSEL_IN), .en(PCWE), .clk(clock_5_out), .Q(PC_OUT));  // open: clr
  Clock clock_5 (.out(clock_5_out));
  Register #(.width(32)) register_1 (
    .D({regs_1_y, regs_1_x}), .en(XYWE), .clk(clock_4_out), .Q({XY_YOUT, XY_XOUT}));  // open: clr
  Hex_Digit_Display hex_digit_display_1 (.value(regs_1_reg0[15:12]));  // open: dp
  Register #(.width(2)) CS (.D(SEGMENT_IN), .en(CSWE), .clk(clock_6_out), .Q(CS_OUT));  // open: clr
  Clock clock_6 (.out(clock_6_out));
  Register #(.width(2)) DS (.D(SEGMENT_IN), .en(DSWE), .clk(clock_7_out), .Q(DS_OUT));  // open: clr
  Clock clock_7 (.out(clock_7_out));
  Hex_Digit_Display hex_digit_display_2 (.value(regs_1_reg0[11:8]));  // open: dp
  Hex_Digit_Display hex_digit_display_3 (.value(regs_1_reg0[7:4]));  // open: dp
  Hex_Digit_Display hex_digit_display_4 (.value(regs_1_reg0[3:0]));  // open: dp
  FSM fsm_1 (
    .CF(CF), .OPCODE(IR_OUT[31:26]), .SF(SF), .OVF(OVF), .ZF(ZF), .SUSPEND(ALUSBY), .PCWE(PCWE),
    .ADRSEL(ADRSEL), .SEGSEL(SEGSEL), .BSSEL(BSSEL), .ARWE(ARWE), .RAMWE(RAMWE), .IRWE(IRWE), .DRWE(DRWE),
    .MEMSSEL(MEMSSEL), .REWSEL(RWSEL), .RWE(RWE), .XYWE(XYWE), .XSEL(XSEL), .YSEL(YSEL), .ALUM(ALUM),
    .ALUWE(ALUWE), .PCSEL(PCSEL), .CSWE(CSWE), .DSWE(DSWE), .DSEL(DSEL));
  Multiplexer #(.select(2), .width(16)) multiplexer_7 (
    .in0(XY_XOUT), .in1(PC_OUT), .in2({16{1'b0}}), .out(multiplexer_7_out), .sel(XSEL));  // open: in3
  Multiplexer #(.select(2), .width(16)) multiplexer_8 (
    .in0(XY_YOUT), .in1({16{1'b0}}), .in2(16'h1), .out(multiplexer_8_out), .sel(YSEL));  // open: in3
  Multiplexer #(.width(2)) multiplexer_9 (.in0(CS_OUT), .in1(DS_OUT), .out(MEM_ADDR), .sel(SEGSEL));
  SignXTND8to16U signxtnd8to16u_1 (.Inp(DR_LOW[7:0]), .Oup(SEU_OUT));
  SignXTND8to16 signxtnd8to16_1 (.Inp(DR_LOW[7:0]), .Oup(SES_OUT));
  Clock clock_8 (.out(clock_8_out));
  Register #(.width(32)) register_2 (
    .D(ALUOUT), .en(ALUWE), .clk(clock_8_out), .Q({ALUREG_HIGH, ALUREG_LOW}));  // open: clr
  ALU alu_1 (
    .ALUM(ALUM), .A(multiplexer_7_out), .B(multiplexer_8_out), .CF(CF), .SF(SF), .ZF(ZF), .OVF(OVF),
    .oup(ALUOUT), .ALUSBY(ALUSBY));
  Register #(.width(16)) AR (.D(AR_IN), .en(ARWE), .clk(clock_9_out), .Q(AR_OUT));  // open: clr
  Clock clock_9 (.out(clock_9_out));
  Multiplexer #(.width(5)) multiplexer_10 (.in0(IR_OUT[25:21]), .in1(AR_IN[15:11]), .out(DEST), .sel(DSEL));

  // Other names for the same wires on the sheet: ALUOUT_LOW[15:0] = ALUOUT[15:0];
  //   ALUREG_LOW_LOW[7:0] = ALUREG_LOW[7:0]; ALUREG_OUT[31:0] = {ALUREG_HIGH, ALUREG_LOW};
  //   DR_LOW_LOW[7:0] = DR_LOW[7:0]; DR_OUT[31:0] = {DR_HIGH, DR_LOW}; DR_LOW_HIGH[7:0] = DR_LOW[15:8];
  //   RAMADR[31:0] = {DR_HIGH, BSMUX}; IR_OUT[15:0] = AR_IN; RADRDEST[4:0] = AR_IN[15:11]; RADRY[4:0] = IR_OUT[20:16];
  //   RADRX[4:0] = IR_OUT[25:21]; OPCODE[5:0] = IR_OUT[31:26]; MEM_ADDR[15:0] = ADR_MUX; SEG_MUX[1:0] = MEM_ADDR

  // Notes on the sheet:
  //   contents of rom_1 (hex, n*v repeats v):
  //   0 2de00054 2c200011 1c410000 2c600011 8430054 2c201234 30200000 28400000 8220054 2c200055 34200001
  //   24400001 8220054 2c2000ff 34200001 20400001 2c60ffff 8430054 2c200014 2c40001e 3c220000 2c600032
  //   8230054 2c200032 2c40000a 40220000 2c600028 8230054 2c200005 2c400006 68221800 2c80001e 8240054
  //   2c800000 8640054 2c200064 2c400004 70221800 2c800019 8240054 2c800000 8640054 2c20fffe 2c400005
  //   6c221800 2c80fff6 8240054 2c80ffff 8640054 2c20fff6 2c400002 74221800 2c80fffb 8240054 2c800000
  //   8640054 2c20000a 2c40000a 422003d 39e00000 2c20000a 2c400014 8220041 39e00000 2c200014 2c40000a
  //   10220045 39e00000 2c20000a 2c40000a 14220049 39e00000 2c20000a 2c400014 c22004d 39e00000 2c20000a
  //   2c40000a 18220051 39e00000 2c00600d 2c200053 38200000 2c00dead 2c200056 38200000 0 10201800 4804000
  //   20038000 5*0 10201800 4804000 6100420 26400000 4*0 10201800 4804000 6100420 27400000 4*0 10201800
  //   4804000 420 30000008 4*0 10201800 4804000 20 20018000 4*0 10201800 4804000 60 20018000 4*0 10201800
  //   4804000 a0 20018000 4*0 10201800 4804000 e0 20018000 4*0 10201800 4804000 120 20018000 4*0 10201800
  //   4804000 160 20018000 4*0 10201800 4804000 1a0 20018000 4*0 10201800 4804000 1e0 20018000 4*0
  //   10201800 4804000 220 20018000 4*0 10201800 4804000 260 20018000 4*0 10201800 4804000 2a0 20018000
  //   4*0 10201800 4804000 2e0 18000 20028001 0 0 0 10201800 4804000 320 18000 20028001 0 0 0 10201800
  //   4804000 360 18000 20028001 0 0 0 10201800 4804000 3a0 18000 20028001 0 0 0 10201800 4804000 38420
  //   20000002 4*0 10201800 4804000 38420 20000004 4*0 10201800 4804000 a000000 6100000 20088000 0 0 0
  //   10201800 4804000 a000000 6100000 20048000 0 0 0 10201800 4804000 a000000 6100000 20008000 0 0 0
  //   10201800 4804000 a100420 26400000 4*0 10201800 4804000 a100420 27400000
  //   RAMADR is RAM DATA
  //   RAMOUT
  //   PCSEL MUX
  //   WRITEMUX
  //   REGS_XYREG
  //   X_ALU_A
  //   Y_ALU_B
  //   X_ALU_A
  //   Y_ALU_B
  //   REGS_XYREG
  //   RAMOUT
  //   WRITEMUX
endmodule

module SignXTND (
  input  [15:0] inp,
  output [31:0] oup
);

  Multiplexer #(.width(16)) multiplexer_1 (.in0({16{1'b0}}), .in1({16{1'b1}}), .out(oup[31:16]), .sel(inp[15]));

  assign oup[15:0] = inp;
endmodule

module SignXTND8to16 (
  input  [7:0] Inp,
  output [15:0] Oup
);

  Multiplexer #(.width(8)) multiplexer_1 (.in0({8{1'b0}}), .in1({8{1'b1}}), .out(Oup[15:8]), .sel(Inp[7]));

  assign Oup[7:0] = Inp;
endmodule

module REGS (
  input  [4:0] AdrX,
  input  [4:0] AdrY,
  input  [4:0] Dest,
  input  [15:0] W,
  input  RWE,
  output [15:0] X,
  output [15:0] Y,
  output [15:0] REG0
);

  wire clock_1_out, clock_2_out, clock_3_out, clock_4_out, clock_5_out, clock_6_out, clock_7_out,
       clock_8_out, clock_9_out, clock_10_out, clock_11_out, clock_12_out, clock_13_out, clock_14_out,
       clock_15_out, clock_16_out, demultiplexer_2_out0, demultiplexer_2_out1, demultiplexer_2_out2,
       demultiplexer_2_out3, demultiplexer_2_out4, demultiplexer_2_out5, demultiplexer_2_out6,
       demultiplexer_2_out7, demultiplexer_2_out8, demultiplexer_2_out9, demultiplexer_2_out10,
       demultiplexer_2_out11, demultiplexer_2_out12, demultiplexer_2_out13, demultiplexer_2_out14,
       demultiplexer_2_out15;
  wire [15:0] demultiplexer_1_out0, demultiplexer_1_out1, demultiplexer_1_out2, demultiplexer_1_out3,
       demultiplexer_1_out4, demultiplexer_1_out5, demultiplexer_1_out6, demultiplexer_1_out7,
       demultiplexer_1_out8, demultiplexer_1_out9, demultiplexer_1_out10, demultiplexer_1_out11,
       demultiplexer_1_out12, demultiplexer_1_out13, demultiplexer_1_out14, demultiplexer_1_out15, R1, R2,
       R3, R4, R5, R6, R7, R8, R9, R10, R11, R12, R13, R14, R15;

  Demultiplexer #(.select(5), .width(16)) demultiplexer_1 (
    .out0(demultiplexer_1_out0), .out1(demultiplexer_1_out1), .out2(demultiplexer_1_out2),
    .out3(demultiplexer_1_out3), .out4(demultiplexer_1_out4), .out5(demultiplexer_1_out5),
    .out6(demultiplexer_1_out6), .out7(demultiplexer_1_out7), .out8(demultiplexer_1_out8),
    .out9(demultiplexer_1_out9), .out10(demultiplexer_1_out10), .out11(demultiplexer_1_out11),
    .out12(demultiplexer_1_out12), .out13(demultiplexer_1_out13), .out14(demultiplexer_1_out14),
    .out15(demultiplexer_1_out15), .in(W), .sel(Dest));  // open: out16, out17, out18, out19, out20, out21, out22, out23, out24, out25, out26, out27, out28, out29, out30, out31
  Demultiplexer #(.select(5)) demultiplexer_2 (
    .out0(demultiplexer_2_out0), .out1(demultiplexer_2_out1), .out2(demultiplexer_2_out2),
    .out3(demultiplexer_2_out3), .out4(demultiplexer_2_out4), .out5(demultiplexer_2_out5),
    .out6(demultiplexer_2_out6), .out7(demultiplexer_2_out7), .out8(demultiplexer_2_out8),
    .out9(demultiplexer_2_out9), .out10(demultiplexer_2_out10), .out11(demultiplexer_2_out11),
    .out12(demultiplexer_2_out12), .out13(demultiplexer_2_out13), .out14(demultiplexer_2_out14),
    .out15(demultiplexer_2_out15), .in(RWE), .sel(Dest));  // open: out16, out17, out18, out19, out20, out21, out22, out23, out24, out25, out26, out27, out28, out29, out30, out31
  Register #(.width(16)) register_1 (
    .D(demultiplexer_1_out0), .en(demultiplexer_2_out0), .clk(clock_1_out), .Q(REG0));  // open: clr
  Clock clock_1 (.out(clock_1_out));
  Register #(.width(16)) register_2 (
    .D(demultiplexer_1_out1), .en(demultiplexer_2_out1), .clk(clock_2_out), .Q(R1));  // open: clr
  Clock clock_2 (.out(clock_2_out));
  Register #(.width(16)) register_3 (
    .D(demultiplexer_1_out2), .en(demultiplexer_2_out2), .clk(clock_3_out), .Q(R2));  // open: clr
  Clock clock_3 (.out(clock_3_out));
  Register #(.width(16)) register_4 (
    .D(demultiplexer_1_out3), .en(demultiplexer_2_out3), .clk(clock_4_out), .Q(R3));  // open: clr
  Clock clock_4 (.out(clock_4_out));
  Register #(.width(16)) register_5 (
    .D(demultiplexer_1_out4), .en(demultiplexer_2_out4), .clk(clock_5_out), .Q(R4));  // open: clr
  Clock clock_5 (.out(clock_5_out));
  Register #(.width(16)) register_6 (
    .D(demultiplexer_1_out5), .en(demultiplexer_2_out5), .clk(clock_6_out), .Q(R5));  // open: clr
  Clock clock_6 (.out(clock_6_out));
  Register #(.width(16)) register_7 (
    .D(demultiplexer_1_out6), .en(demultiplexer_2_out6), .clk(clock_7_out), .Q(R6));  // open: clr
  Clock clock_7 (.out(clock_7_out));
  Register #(.width(16)) register_8 (
    .D(demultiplexer_1_out7), .en(demultiplexer_2_out7), .clk(clock_8_out), .Q(R7));  // open: clr
  Clock clock_8 (.out(clock_8_out));
  Register #(.width(16)) register_9 (
    .D(demultiplexer_1_out8), .en(demultiplexer_2_out8), .clk(clock_9_out), .Q(R8));  // open: clr
  Clock clock_9 (.out(clock_9_out));
  Register #(.width(16)) register_10 (
    .D(demultiplexer_1_out9), .en(demultiplexer_2_out9), .clk(clock_10_out), .Q(R9));  // open: clr
  Clock clock_10 (.out(clock_10_out));
  Register #(.width(16)) register_11 (
    .D(demultiplexer_1_out10), .en(demultiplexer_2_out10), .clk(clock_11_out), .Q(R10));  // open: clr
  Clock clock_11 (.out(clock_11_out));
  Register #(.width(16)) register_12 (
    .D(demultiplexer_1_out11), .en(demultiplexer_2_out11), .clk(clock_12_out), .Q(R11));  // open: clr
  Clock clock_12 (.out(clock_12_out));
  Register #(.width(16)) register_13 (
    .D(demultiplexer_1_out12), .en(demultiplexer_2_out12), .clk(clock_13_out), .Q(R12));  // open: clr
  Clock clock_13 (.out(clock_13_out));
  Register #(.width(16)) register_14 (
    .D(demultiplexer_1_out13), .en(demultiplexer_2_out13), .clk(clock_14_out), .Q(R13));  // open: clr
  Clock clock_14 (.out(clock_14_out));
  Register #(.width(16)) register_15 (
    .D(demultiplexer_1_out14), .en(demultiplexer_2_out14), .clk(clock_15_out), .Q(R14));  // open: clr
  Clock clock_15 (.out(clock_15_out));
  Register #(.width(16)) register_16 (
    .D(demultiplexer_1_out15), .en(demultiplexer_2_out15), .clk(clock_16_out), .Q(R15));  // open: clr
  Clock clock_16 (.out(clock_16_out));
  Multiplexer #(.select(5), .width(16)) multiplexer_1 (
    .in0(REG0), .in1(R1), .in2(R2), .in3(R3), .in4(R4), .in5(R5), .in6(R6), .in7(R7), .in8(R8), .in9(R9),
    .in10(R10), .in11(R11), .in12(R12), .in13(R13), .in14(R14), .in15(R15), .out(X), .sel(AdrX));  // open: in16, in17, in18, in19, in20, in21, in22, in23, in24, in25, in26, in27, in28, in29, in30, in31
  Multiplexer #(.select(5), .width(16)) multiplexer_2 (
    .in0(REG0), .in1(R1), .in2(R2), .in3(R3), .in4(R4), .in5(R5), .in6(R6), .in7(R7), .in8(R8), .in9(R9),
    .in10(R10), .in11(R11), .in12(R12), .in13(R13), .in14(R14), .in15(R15), .out(Y), .sel(AdrY));  // open: in16, in17, in18, in19, in20, in21, in22, in23, in24, in25, in26, in27, in28, in29, in30, in31

  // Other names for the same wires on the sheet: R0[15:0] = REG0

  // Notes on the sheet:
  //   written data demux
  //   write enable demux
  //   x_mux
  //   y_mux
endmodule

module SignXTND8to16U (
  input  [7:0] Inp,
  output [15:0] Oup
);


  assign Oup = {{8{1'b0}}, Inp};
endmodule

module FSM (
  input  CF,
  input  [5:0] OPCODE,
  input  SF,
  input  OVF,
  input  ZF,
  input  SUSPEND,
  output PCWE,
  output [1:0] ADRSEL,
  output SEGSEL,
  output BSSEL,
  output ARWE,
  output RAMWE,
  output IRWE,
  output DRWE,
  output [1:0] MEMSSEL,
  output [1:0] REWSEL,
  output RWE,
  output XYWE,
  output [1:0] XSEL,
  output [1:0] YSEL,
  output [3:0] ALUM,
  output ALUWE,
  output [1:0] PCSEL,
  output CSWE,
  output DSWE,
  output DSEL
);

  wire and_1_out, and_2_out, and_3_out, and_4_out, and_5_out, and_6_out, clock_1_out, d_ff_1_q,
       flagjump_module_1_jumpout, jumptoconsider_module_1_is_jump, not_1_out, not_2_out;
  wire [1:0] multiplexer_1_out, rom_1_data;
  wire [2:0] t_ff_1_q;
  wire [29:29] rom_1_data_2;

  and and_1 (and_1_out, 1'b1, not_1_out);
  Clock clock_1 (.out(clock_1_out));
  not not_1 (not_1_out, SUSPEND);
  T_Flip_Flop t_ff_1 (.T(and_1_out), .clk(clock_1_out), .Q(t_ff_1_q[0]), .reset(and_5_out));  // open: Qn, preset
  ROM #(.addrWidth(9), .dataWidth(30)) rom_1 (
    .addr({OPCODE, t_ff_1_q}),
    .data({rom_1_data_2[29], PCWE, ADRSEL, SEGSEL, BSSEL, ARWE, RAMWE, IRWE, DRWE, MEMSSEL, REWSEL, RWE, XYWE, XSEL, YSEL, ALUM, ALUWE, rom_1_data, CSWE, DSWE, DSEL}));
  T_Flip_Flop t_ff_2 (.T(and_2_out), .clk(clock_1_out), .Q(t_ff_1_q[1]), .reset(and_5_out));  // open: Qn, preset
  and and_2 (and_2_out, t_ff_1_q[0], not_1_out);
  T_Flip_Flop t_ff_3 (.T(and_3_out), .clk(clock_1_out), .Q(t_ff_1_q[2]), .reset(and_5_out));  // open: Qn, preset
  and and_3 (and_3_out, t_ff_1_q[0], t_ff_1_q[1], not_1_out);
  and and_4 (and_4_out, ~t_ff_1_q[0], ~t_ff_1_q[1], ~t_ff_1_q[2]);  // AND_Gate
  not not_2 (not_2_out, and_4_out);
  and and_5 (and_5_out, not_2_out, d_ff_1_q);
  D_Flip_Flop d_ff_1 (.D(rom_1_data_2[29]), .clk(clock_1_out), .Q(d_ff_1_q));  // open: Qn, preset, reset
  Multiplexer #(.width(2)) multiplexer_1 (
    .in0(2'b10), .in1(2'b11), .out(multiplexer_1_out), .sel(flagjump_module_1_jumpout));
  FLAGJUMP_Module flagjump_module_1 (
    .SF(SF), .OVF(OVF), .ZF(ZF), .JMPSELECT(OPCODE[2:0]), .JUMPOUT(flagjump_module_1_jumpout));
  JUMPTOCONSIDER_MODULE jumptoconsider_module_1 (.OPCODE(OPCODE), .IS_JUMP(jumptoconsider_module_1_is_jump));
  Multiplexer #(.width(2)) multiplexer_2 (.in0(rom_1_data), .in1(multiplexer_1_out), .out(PCSEL), .sel(and_6_out));
  and and_6 (and_6_out, jumptoconsider_module_1_is_jump, ~IRWE);  // AND_Gate

  // Notes on the sheet:
  //   contents of rom_1 (hex, n*v repeats v):
  //   10201800 4804000 20000000 5*0 10201800 4804000 800060 30000040 4*0 10201800 4804000 800060 30000040
  //   4*0 10201800 4804000 800060 30000040 4*0 10201800 4804000 800060 30000040 4*0 10201800 4804000
  //   800060 30000040 4*0 10201800 4804000 800060 30000040 4*0 10201800 4804000 2020 20018000 4*0 10201800
  //   4804000 6000000 6100000 20088000 0 0 0 10201800 4804000 6000000 6100000 20048000 0 0 0 10201800
  //   4804000 6000000 6100000 20008000 0 0 0 10201800 4804000 20038000 5*0 10201800 4804000 6100420
  //   26400000 4*0 10201800 4804000 6100420 27400000 4*0 10201800 4804000 420 30000008 4*0 10201800
  //   4804000 20 20018000 4*0 10201800 4804000 60 20018000 4*0 10201800 4804000 a0 20018000 4*0 10201800
  //   4804000 e0 20018000 4*0 10201800 4804000 120 20018000 4*0 10201800 4804000 160 20018000 4*0 10201800
  //   4804000 1a0 20018000 4*0 10201800 4804000 1e0 20018000 4*0 10201800 4804000 220 20018000 4*0
  //   10201800 4804000 260 20018000 4*0 10201800 4804000 2a0 20018000 4*0 10201800 4804000 2e0 18000
  //   20028001 0 0 0 10201800 4804000 320 18000 20028001 0 0 0 10201800 4804000 360 18000 20028001 0 0 0
  //   10201800 4804000 3a0 18000 20028001 0 0 0 10201800 4804000 38420 20000002 4*0 10201800 4804000 38420
  //   20000004 4*0 10201800 4804000 a000000 6100000 20088000 0 0 0 10201800 4804000 a000000 6100000
  //   20048000 0 0 0 10201800 4804000 a000000 6100000 20008000 0 0 0 10201800 4804000 6100420 2a400000 4*0
  //   10201800 4804000 6100420 2b400000
  //   FSM counter
  //   PC = PC
  //   PC = JMP_ADDR
  //   JUMP RESULT MUX
  //   JUMP CONSIDER MUX
endmodule

module BACKUPFSM (
  input  CF,
  input  SF,
  input  OVF,
  input  [5:0] OPCODE,
  input  ZF,
  output out_6,
  output [1:0] out_7,
  output out_8,
  output out_9,
  output PCWE,
  output out_11,
  output [1:0] ADRSEL,
  output out_13,
  output SEGSEL,
  output out_15,
  output BSSEL,
  output out_17,
  output ARWE,
  output [1:0] out_19,
  output RAMWE,
  output [1:0] out_21,
  output IRWE,
  output out_23,
  output DRWE,
  output out_25,
  output [1:0] MEMSSEL,
  output [1:0] out_27,
  output [1:0] REWSEL,
  output [1:0] out_29,
  output RWE,
  output [3:0] out_31,
  output XYWE,
  output out_33,
  output [1:0] XSEL,
  output [1:0] out_35,
  output [1:0] YSEL,
  output out_37,
  output [3:0] ALUM,
  output out_39,
  output ALUWE,
  output [1:0] PCSEL,
  output CSWE,
  output DSWE
);

  wire and_1_out, and_2_out, clock_1_out, comparator_1_lt, d_ff_1_q, multiplexer_1_out, not_1_out, or_1_out,
       xnor_1_out, xor_1_out;
  wire [1:0] multiplexer_2_out, rom_1_data_2, rom_1_data_3, rom_1_data_4, rom_1_data_5, rom_1_data_6,
       rom_1_data_8, undriven;
  wire [2:0] t_ff_1_q;
  wire [3:0] rom_1_data_7;
  wire [28:0] rom_1_data;

  Clock clock_1 (.out(clock_1_out));
  T_Flip_Flop t_ff_1 (.T(1'b1), .clk(clock_1_out), .Q(t_ff_1_q[0]), .reset(d_ff_1_q));  // open: Qn, preset
  ROM #(.addrWidth(9), .dataWidth(29)) rom_1 (
    .addr({OPCODE, t_ff_1_q}),
    .data({rom_1_data[28:26], rom_1_data_8, rom_1_data[23], rom_1_data_7, rom_1_data_6, rom_1_data_5, rom_1_data[14:13], rom_1_data_4, rom_1_data_3, rom_1_data[8:3], rom_1_data_2, rom_1_data[0]}));
  T_Flip_Flop t_ff_2 (.T(t_ff_1_q[0]), .clk(clock_1_out), .Q(t_ff_1_q[1]), .reset(d_ff_1_q));  // open: Qn, preset
  T_Flip_Flop t_ff_3 (.T(and_1_out), .clk(clock_1_out), .Q(t_ff_1_q[2]), .reset(d_ff_1_q));  // open: Qn, preset
  and and_1 (and_1_out, t_ff_1_q[0], t_ff_1_q[1]);
  D_Flip_Flop d_ff_1 (.D(rom_1_data[28]), .clk(clock_1_out), .Q(d_ff_1_q));  // open: Qn, preset, reset
  Comparator #(.mode("unsigned"), .width(6)) comparator_1 (
    .a(OPCODE), .b(6'b000110), .lt(comparator_1_lt));  // open: gt, eq
  xnor xnor_1 (xnor_1_out, SF, OVF);
  xor xor_1 (xor_1_out, SF, OVF);
  not not_1 (not_1_out, ZF);
  or or_1 (or_1_out, xor_1_out, ZF);
  and and_2 (and_2_out, xnor_1_out, not_1_out);
  Multiplexer #(.select(3)) multiplexer_1 (
    .in0(ZF), .in1(not_1_out), .in2(xor_1_out), .in3(and_2_out), .in4(xnor_1_out), .in5(or_1_out),
    .in6(1'b0), .in7(1'b0), .out(multiplexer_1_out), .sel(OPCODE[2:0]));
  Multiplexer #(.width(2)) multiplexer_2 (.in0(2'b00), .in1(2'b01), .out(multiplexer_2_out), .sel(multiplexer_1_out));
  Multiplexer #(.width(2)) multiplexer_3 (.in0(undriven), .in1(multiplexer_2_out), .out(PCSEL), .sel(comparator_1_lt));

  // Notes on the sheet:
  //   contents of rom_1 (hex, n*v repeats v):
  //   8100c00 402000 400030 18000000 4*0 8100c00 402000 400030 18000000 4*0 8100c00 402000 400030 18000000
  //   4*0 8100c00 402000 400030 18000000 4*0 8100c00 402000 400030 18000000 4*0 8100c00 402000 400030
  //   18000000 4*0 8100c00 402000 1010 1000c000 4*0 8100c00 402000 3080000 10044000 4*0 8100c00 402000
  //   3080000 10024000 4*0 8100c00 402000 3080000 10004000 4*0 8100c00 402000 1001c000 5*0 8100c00 402000
  //   3080210 13200000 4*0 8100c00 402000 3080210 13a00000 4*0 8100c00 402000 210 18000004 4*0 8100c00
  //   402000 10 1000c000 4*0 8100c00 402000 30 1000c000 4*0 8100c00 402000 50 1000c000 4*0 8100c00 402000
  //   70 1000c000 4*0 8100c00 402000 90 1000c000 4*0 8100c00 402000 b0 1000c000 4*0 8100c00 402000 d0
  //   1000c000 4*0 8100c00 402000 f0 1000c000 4*0 8100c00 402000 110 1000c000 4*0 8100c00 402000 130
  //   1000c000 4*0 8100c00 402000 150 1000c000 4*0 8100c00 402000 170 1000c000 4*0 8100c00 402000 190
  //   1000c000 4*0 8100c00 402000 1b0 1000c000 4*0 8100c00 402000 1d0 1000c000 4*0 8100c00 402000 10000000
endmodule

module FLAGJUMP_Module (
  input  SF,
  input  OVF,
  input  ZF,
  input  [2:0] JMPSELECT,
  output JUMPOUT
);

  wire and_1_out, not_1_out, or_1_out, xnor_1_out, xor_1_out;

  xor xor_1 (xor_1_out, SF, OVF);
  xnor xnor_1 (xnor_1_out, OVF, SF);
  not not_1 (not_1_out, ZF);
  or or_1 (or_1_out, xor_1_out, ZF);
  and and_1 (and_1_out, xnor_1_out, not_1_out);
  Multiplexer #(.select(3)) multiplexer_1 (
    .in0(1'b0), .in1(ZF), .in2(not_1_out), .in3(xor_1_out), .in4(and_1_out), .in5(xnor_1_out),
    .in6(or_1_out), .in7(1'b0), .out(JUMPOUT), .sel(JMPSELECT));
endmodule

module JUMPTOCONSIDER_MODULE (
  input  [5:0] OPCODE,
  output IS_JUMP
);

  wire comparator_1_lt, comparator_2_eq, not_1_out;

  Comparator #(.mode("unsigned"), .width(6)) comparator_1 (
    .a(OPCODE), .b(6'b000111), .lt(comparator_1_lt));  // open: gt, eq
  Comparator #(.mode("unsigned"), .width(6)) comparator_2 (
    .a(OPCODE), .b({6{1'b0}}), .eq(comparator_2_eq));  // open: gt, lt
  and and_1 (IS_JUMP, comparator_1_lt, not_1_out);
  not not_1 (not_1_out, comparator_2_eq);
endmodule

module DIV (
  input  [15:0] DIVISOR,
  input  [15:0] DIVIDEND,
  input  START,
  input  RESET,
  output ALUSBY,
  output [15:0] QUOTENT,
  output [15:0] REMAINDER
);

  wire and_1_out, and_2_out, clock_1_out, clock_2_out, comparator_1_eq, comparator_2_eq, comparator_2_gt,
       d_ff_1_q, d_ff_1_qn, HIGHBGREATER, not_1_out, not_2_out, or_1_out;
  wire [4:0] counter_1_q;
  wire [15:0] subtractor_1_out;
  wire [31:0] multiplexer_1_out;
  wire [31:16] multiplexer_2_out;

  Clock clock_1 (.out(clock_1_out));
  not not_1 (not_1_out, START);
  Counter #(.max('h1f), .width(5)) counter_1 (
    .clr(or_1_out), .load(and_1_out), .up(1'b0), .count(1'b1), .clk(clock_1_out), .D(5'b10000),
    .Q(counter_1_q));  // open: carry
  or or_1 (or_1_out, RESET, not_1_out);
  and and_1 (and_1_out, START, comparator_1_eq);
  D_Flip_Flop d_ff_1 (.D(START), .clk(clock_2_out), .Q(d_ff_1_q), .Qn(d_ff_1_qn));  // open: preset, reset
  Clock clock_2 (.out(clock_2_out));
  not not_2 (not_2_out, comparator_1_eq);
  Comparator #(.mode("unsigned"), .width(5)) comparator_1 (
    .a(counter_1_q), .b({5{1'b0}}), .eq(comparator_1_eq));  // open: gt, lt
  and and_2 (and_2_out, START, d_ff_1_qn);
  or or_2 (ALUSBY, and_2_out, not_2_out);
  Multiplexer #(.width(32)) multiplexer_1 (
    .in0({{16{1'b0}}, DIVIDEND}), .in1({multiplexer_2_out, QUOTENT[14:0], HIGHBGREATER}),
    .out(multiplexer_1_out), .sel(d_ff_1_q));
  Register #(.width(32)) register_1 (
    .D(multiplexer_1_out), .en(1'b1), .clk(clock_1_out), .Q({REMAINDER, QUOTENT}), .clr(RESET));
  Multiplexer #(.width(16)) multiplexer_2 (
    .in0({REMAINDER[14:0], QUOTENT[15]}), .in1(subtractor_1_out), .out(multiplexer_2_out), .sel(HIGHBGREATER));
  Comparator #(.mode("unsigned"), .width(16)) comparator_2 (
    .a({REMAINDER[14:0], QUOTENT[15]}), .b(DIVISOR), .gt(comparator_2_gt), .eq(comparator_2_eq));  // open: lt
  or or_3 (HIGHBGREATER, comparator_2_gt, comparator_2_eq);
  Subtractor #(.width(16)) subtractor_1 (
    .a({REMAINDER[14:0], QUOTENT[15]}), .b(DIVISOR), .out(subtractor_1_out), .bin(1'b0));  // open: bout

  // Notes on the sheet:
  //   Shift logic
  //   HIGH Bits checked against DIVISOR
endmodule
